# Fritzing sketch arduino mobo (saved by Fritzing 0.9.3b)
circuit board: 7.5cm x 8cm
breadboards: 1

parts:
  J9 = screw terminal, 2 pins
  Part2 = Arduino Micro (Rev3)
  LOGIC5 = female pin header, 2 pins [form="♀ (female)"]
  LOGIC19 = female pin header, 4 pins [form="♀ (female)"]  # not connected
  LOGIC21 = female pin header, 4 pins [form="♀ (female)"]
  LOGIC24 = female pin header, 3 pins [form="♀ (female)"]
  U5 = mystery part, 16 pins [chip_label=STEPPER]
  C4 = Electrolytic Capacitor [capacitance=0.47mF voltage=35V package="100 mil [THT, electrolytic]"]
  LOGIC25 = female pin header, 3 pins [form="♀ (female)"]
  LOGIC26 = female pin header, 3 pins [form="♀ (female)"]
  LOGIC27 = female pin header, 3 pins [form="♀ (female)"]
  LOGIC28 = female pin header, 3 pins [form="♀ (female)"]
  LOGIC29 = female pin header, 3 pins [form="♀ (female)"]
  LOGIC30 = female pin header, 3 pins [form="♀ (female)"]
  LOGIC31 = female pin header, 3 pins [form="♀ (female)"]
  LOGIC32 = female pin header, 4 pins [form="♀ (female)"]
  U6 = mystery part, 16 pins [chip_label=STEPPER]
  C5 = Electrolytic Capacitor [capacitance=0.47mF voltage=35V package="100 mil [THT, electrolytic]"]
  LOGIC33 = female pin header, 4 pins [form="♀ (female)"]
  U7 = mystery part, 16 pins [chip_label=STEPPER]
  C6 = Electrolytic Capacitor [capacitance=0.47mF voltage=35V package="100 mil [THT, electrolytic]"]
  C7 = Electrolytic Capacitor [capacitance=0.47mF voltage=35V package="100 mil [THT, electrolytic]"]
  C8 = Electrolytic Capacitor [capacitance=0.47mF voltage=35V package="100 mil [THT, electrolytic]"]
  C9 = Electrolytic Capacitor [capacitance=0.47mF voltage=35V package="100 mil [THT, electrolytic]"]

nets:
  N1: J9.pin1, Part2.GND, LOGIC24.pin3, U5.pin7, C4.-, LOGIC25.pin3, LOGIC26.pin3, LOGIC27.pin3, LOGIC28.pin3, LOGIC29.pin3, LOGIC30.pin3, LOGIC31.pin3, U6.pin7, C5.-, U7.pin7, C6.-, C7.-, C8.-, C9.-
  N2: J9.pin2, U5.pin8, C4.+, U6.pin8, C5.+, U7.pin8, C6.+, C7.+
  N3: Part2.D2/SDA, LOGIC5.pin1
  N4: Part2.D3/SCL, LOGIC5.pin2
  N5: Part2.D4_PWM/A6, U5.pin16
  N6: Part2.D5_PWM, U5.pin15
  N7: Part2.D6_PWM/A7, U6.pin16
  N8: Part2.D7, U6.pin15
  N9: Part2.D8_PWM/A8, U7.pin16
  N10: Part2.D9_PWM/A9, U7.pin15
  N11: Part2.D10_PWM/A10, LOGIC25.pin1
  N12: Part2.D12_PWM/A11, LOGIC24.pin1
  N13: Part2.5V, LOGIC24.pin2, LOGIC25.pin2, LOGIC26.pin2, LOGIC27.pin2, LOGIC28.pin2, LOGIC29.pin2, LOGIC30.pin2, LOGIC31.pin2, U7.pin2, C8.+, C9.+
  N14: Part2.A5, LOGIC28.pin1
  N15: Part2.A4, LOGIC29.pin1
  N16: Part2.A3, LOGIC30.pin1
  N17: Part2.A2, LOGIC31.pin1
  N18: Part2.A1, LOGIC26.pin1
  N19: Part2.A0, LOGIC27.pin1
  N20: LOGIC21.pin1, U5.pin6
  N21: LOGIC21.pin2, U5.pin5
  N22: LOGIC21.pin3, U5.pin4
  N23: LOGIC21.pin4, U5.pin3
  N24: LOGIC32.pin1, U6.pin6
  N25: LOGIC32.pin2, U6.pin5
  N26: LOGIC32.pin3, U6.pin4
  N27: LOGIC32.pin4, U6.pin3
  N28: LOGIC33.pin1, U7.pin6
  N29: LOGIC33.pin2, U7.pin5
  N30: LOGIC33.pin3, U7.pin4
  N31: LOGIC33.pin4, U7.pin3

notes:
  SDA
  SCL
  9V
  + -
