# Fritzing sketch motherboard-v5 (saved by Fritzing 0.9.3b)
circuit board: 8cm x 8cm
breadboards: 1

parts:
  J1 = Infrared Proximity Sensor
  J2 = Infrared Proximity Sensor
  J3 = Infrared Proximity Sensor
  J5 = Infrared Proximity Sensor
  J6 = Infrared Proximity Sensor
  C1 = Electrolytic Capacitor [capacitance=1µF package="100 mil [THT, electrolytic]"]
  C2 = Electrolytic Capacitor [capacitance=1µF package="100 mil [THT, electrolytic]"]
  J4 = Infrared Proximity Sensor
  C3 = Electrolytic Capacitor [capacitance=1µF package="100 mil [THT, electrolytic]"]
  FRONT_LEFT = mystery part, 16 pins [chip_label=?]  # not connected
  FRONT_RIGHT = mystery part, 16 pins [chip_label=?]  # not connected
  BACK = mystery part, 16 pins [chip_label=?]  # not connected
  C4 = Electrolytic Capacitor [capacitance=47µF package="100 mil [THT, electrolytic]"]
  C5 = Electrolytic Capacitor [capacitance=47µF package="100 mil [THT, electrolytic]"]
  C6 = Electrolytic Capacitor [capacitance=47µF package="100 mil [THT, electrolytic]"]
  J9 = screw terminal, 2 pins
  C7 = Electrolytic Capacitor [capacitance=1µF package="100 mil [THT, electrolytic]"]
  Arduino_Micro = Arduino Micro (Rev3)
  BACK_2 = male pin header, 4 pins [form="♂ (male)"]  # not connected
  RIGHT = male pin header, 4 pins [form="♂ (male)"]  # not connected
  LEFT = male pin header, 4 pins [form="♂ (male)"]  # not connected
  I2C = female pin header, 2 pins [form="♀ (female)"]

nets:
  N1: J1.Vout, J2.Vout, C1.-
  GND: J1.GND, J2.GND, C1.+
  N2: J3.Vout, J4.Vout, C3.-
  GND_2: J3.GND, J4.GND, C3.+
  N3: J5.Vout, J6.Vout, C2.-
  GND_3: J5.GND, J6.GND, C2.+
  N4: C4.-, C5.-, C6.-, J9.pin1
  N5: C4.+, J9.pin2
  N6: C7.-, Arduino_Micro.GND
  N7: C7.+, Arduino_Micro.VIN
  N8: Arduino_Micro.D2/SDA, I2C.pin1
  N9: Arduino_Micro.D3/SCL, I2C.pin2

notes:
  USB in
  motherboard v5
  github.com/timmd909/catpoo
  + -
