# Fritzing sketch motherboard (saved by Fritzing 0.9.2b)
circuit board: 8.25cm x 9.6cm
breadboards: 1

parts:
  VOUT+ = male pin header, 5 pins [form="♂ (male)"]
  VOUT- = male pin header, 5 pins [form="♂ (male)"]
  D3 = Rectifier Diode [part_number=1N4001 package="300 mil [THT]"]
  WALL = male pin header, 2 pins [form="♂ (male)"]
  BATT = male pin header, 2 pins [form="♂ (male)"]
  D1 = Rectifier Diode [part_number=1N4001 package="300 mil [THT]"]
  D2 = Rectifier Diode [part_number=1N4001 package="300 mil [THT]"]
  SWITCH_IN = mystery part, 2 pins [chip_label=?]
  SWITCH_OUT = mystery part, 4 pins [chip_label=?]
  FL-C = Electrolytic Capacitor [capacitance=1µF package="100 mil [THT, electrolytic]"]
  BL-C = Electrolytic Capacitor [capacitance=1µF package="100 mil [THT, electrolytic]"]
  FR-C = Electrolytic Capacitor [capacitance=1µF package="100 mil [THT, electrolytic]"]
  BR-C = Electrolytic Capacitor [capacitance=1µF package="100 mil [THT, electrolytic]"]
  BL_MOTOR = male pin header, 4 pins [form="♂ (male)"]
  FL_MOTOR = male pin header, 4 pins [form="♂ (male)"]
  BR_MOTOR = male pin header, 4 pins [form="♂ (male)"]
  FR_MOTOR = male pin header, 4 pins [form="♂ (male)"]
  5V-I2C = male pin header, 2 pins [form="♂ (male)"]
  FL_DRIVER = mystery part, 16 pins [chip_label=?]
  BL_DRIVER = mystery part, 16 pins [chip_label=?]
  BR_DRIVER = mystery part, 16 pins [chip_label=?]
  MOTOR_PWR = male pin header, 2 pins [form="♂ (male)"]
  5V+ = male pin header, 6 pins [form="♂ (male)"]
  5V- = male pin header, 6 pins [form="♂ (male)"]
  3V+ = male pin header, 6 pins [form="♂ (male)"]
  3V- = male pin header, 6 pins [form="♂ (male)"]
  FR_DRIVER = mystery part, 16 pins [chip_label=?]
  A0 = male pin header, 3 pins [form="♂ (male)"]
  A1 = male pin header, 3 pins [form="♂ (male)"]
  A2 = male pin header, 3 pins [form="♂ (male)"]
  A3 = male pin header, 3 pins [form="♂ (male)"]
  A4 = male pin header, 3 pins [form="♂ (male)"]
  A5 = male pin header, 3 pins [form="♂ (male)"]
  ARDUINO = mystery part, 34 pins [chip_label=?]
  5V-C1 = Electrolytic Capacitor [capacitance=1µF package="100 mil [THT, electrolytic]"]
  5V-C2 = Electrolytic Capacitor [capacitance=1µF package="100 mil [THT, electrolytic]"]
  3V-C3 = Electrolytic Capacitor [capacitance=1µF package="100 mil [THT, electrolytic]"]
  STEPPER_OPTIONS7 = male pin header, 4 pins [form="♂ (male)"]  # not connected
  STEPPER_OPTIONS8 = male pin header, 4 pins [form="♂ (male)"]  # not connected
  STEPPER_OPTIONS9 = male pin header, 4 pins [form="♂ (male)"]  # not connected
  STEPPER_OPTIONS10 = male pin header, 4 pins [form="♂ (male)"]  # not connected
  ARDUINO_PWR = male pin header, 2 pins [form="♂ (male)"]

nets:
  N1: VOUT+.pin1, VOUT+.pin2, VOUT+.pin3, VOUT+.pin4, VOUT+.pin5, D1.cathode, D2.cathode
  N2: VOUT-.pin1, VOUT-.pin2, VOUT-.pin3, VOUT-.pin4, VOUT-.pin5, D3.anode
  N3: D3.cathode, WALL.pin2, BATT.pin2
  N4: WALL.pin1, SWITCH_IN.pin1
  N5: BATT.pin1, SWITCH_IN.pin2, SWITCH_OUT.pin1
  N6: D1.anode, SWITCH_OUT.pin4
  N7: D2.anode, SWITCH_OUT.pin2
  N8: FL-C.-, BL-C.-, FR-C.-, BR-C.-, FL_DRIVER.pin7, BL_DRIVER.pin7, BR_DRIVER.pin7, MOTOR_PWR.pin2, FR_DRIVER.pin7
  N9: FL-C.+, BL-C.+, FR-C.+, BR-C.+, FL_DRIVER.pin8, BL_DRIVER.pin8, BR_DRIVER.pin8, MOTOR_PWR.pin1, FR_DRIVER.pin8
  N10: BL_MOTOR.pin1, BL_DRIVER.pin3
  N11: BL_MOTOR.pin2, BL_DRIVER.pin4
  N12: BL_MOTOR.pin3, BL_DRIVER.pin5
  N13: BL_MOTOR.pin4, BL_DRIVER.pin6
  N14: FL_MOTOR.pin1, FL_DRIVER.pin3
  N15: FL_MOTOR.pin2, FL_DRIVER.pin4
  N16: FL_MOTOR.pin3, FL_DRIVER.pin5
  N17: FL_MOTOR.pin4, FL_DRIVER.pin6
  N18: BR_MOTOR.pin1, BR_DRIVER.pin3
  N19: BR_MOTOR.pin2, BR_DRIVER.pin4
  N20: BR_MOTOR.pin3, BR_DRIVER.pin5
  N21: BR_MOTOR.pin4, BR_DRIVER.pin6
  N22: FR_MOTOR.pin1, FR_DRIVER.pin3
  N23: FR_MOTOR.pin2, FR_DRIVER.pin4
  N24: FR_MOTOR.pin3, FR_DRIVER.pin5
  N25: FR_MOTOR.pin4, FR_DRIVER.pin6
  N26: 5V-I2C.pin1, ARDUINO.pin24
  N27: 5V-I2C.pin2, ARDUINO.pin25
  N28: FL_DRIVER.pin1, BL_DRIVER.pin1, BR_DRIVER.pin1, 5V-.pin1, 5V-.pin2, 5V-.pin3, 5V-.pin4, 5V-.pin5, 5V-.pin6, 3V-.pin1, 3V-.pin2, 3V-.pin3, 3V-.pin4, 3V-.pin5, 3V-.pin6, FR_DRIVER.pin1, A0.pin1, A1.pin1, A2.pin1, A3.pin1, A4.pin1, A5.pin1, ARDUINO.pin14, ARDUINO.pin23, 5V-C1.-, 5V-C2.-, 3V-C3.-, ARDUINO_PWR.pin1
  N29: FL_DRIVER.pin2, FL_DRIVER.pin14, BL_DRIVER.pin2, BL_DRIVER.pin14, BR_DRIVER.pin2, BR_DRIVER.pin14, 5V+.pin1, 5V+.pin2, 5V+.pin3, 5V+.pin4, 5V+.pin5, 5V+.pin6, FR_DRIVER.pin2, FR_DRIVER.pin14, A0.pin2, A1.pin2, A2.pin2, A3.pin2, A4.pin2, A5.pin2, ARDUINO.pin12, 5V-C1.+, 5V-C2.+
  N30: FL_DRIVER.pin15, ARDUINO.pin29
  N31: FL_DRIVER.pin16, ARDUINO.pin28
  N32: BL_DRIVER.pin15, ARDUINO.pin31
  N33: BL_DRIVER.pin16, ARDUINO.pin30
  N34: BR_DRIVER.pin15, ARDUINO.pin32
  N35: BR_DRIVER.pin16, ARDUINO.pin33
  N36: 3V+.pin1, 3V+.pin2, 3V+.pin3, 3V+.pin4, 3V+.pin5, 3V+.pin6, ARDUINO.pin2, 3V-C3.+
  N37: FR_DRIVER.pin15, ARDUINO.pin26
  N38: FR_DRIVER.pin16, ARDUINO.pin27
  N39: A0.pin3, ARDUINO.pin4
  N40: A1.pin3, ARDUINO.pin5
  N41: A2.pin3, ARDUINO.pin6
  N42: A3.pin3, ARDUINO.pin7
  N43: A4.pin3, ARDUINO.pin8
  N44: A5.pin3, ARDUINO.pin9
  N45: ARDUINO.pin15, ARDUINO_PWR.pin2

notes:
  POWER SUPPLY CIRCUIT
  FR MOTOR
  tim-doerzbacher.com
  FL MOTOR
  BL MOTOR
  BR MOTOR
  ARDUINO
  POWER SUPPLY
  CATPOO
  motherboard v2
  github.com/timmd909/catpoo
  PWR
  SIG
  GND
  +
  SDA
  SCL
