# Fritzing sketch motor shield (saved by Fritzing 0.9.2b)
circuit board: 10.6663cm x 6.47989cm
breadboards: 5

parts:
  FR_MOTOR = female pin header, 4 pins [form="♀ (female)"]
  BR_MOTOR = female pin header, 4 pins [form="♀ (female)"]
  FL_MOTOR = female pin header, 4 pins [form="♀ (female)"]
  BL_MOTOR = female pin header, 4 pins [form="♀ (female)"]
  FR_DRIVER = A4988 Stepper Motor Driver Carrier
  BR_DRIVER = A4988 Stepper Motor Driver Carrier
  FL_DRIVER = A4988 Stepper Motor Driver Carrier
  BL_DRIVER = A4988 Stepper Motor Driver Carrier
  MOTOR_PWR = female pin header, 2 pins [form="♀ (female)"]
  +5V-2 = female pin header, 2 pins [form="♀ (female)"]
  +5V-1 = female pin header, 2 pins [form="♀ (female)"]
  ARDUINO_PWR = female pin header, 2 pins [form="♀ (female)"]
  +5V-3 = female pin header, 2 pins [form="♀ (female)"]
  +5V-4 = female pin header, 2 pins [form="♀ (female)"]
  +5V-5 = female pin header, 2 pins [form="♀ (female)"]
  ARDUINO_MICRO2 = Arduino Micro
  BR_CAP = Capacitor Polarized [package=panasonic_e]
  FR_CAP = Capacitor Polarized [package=panasonic_e]
  BL_CAP = Capacitor Polarized [package=panasonic_e]
  I2C_5V = female pin header, 2 pins [form="♀ (female)"]
  AIN1 = female pin header, 3 pins [form="♀ (female)"]
  AIN2 = female pin header, 3 pins [form="♀ (female)"]
  AIN4 = female pin header, 3 pins [form="♀ (female)"]
  AIN5 = female pin header, 3 pins [form="♀ (female)"]
  AIN6 = female pin header, 3 pins [form="♀ (female)"]
  AIN3 = female pin header, 3 pins [form="♀ (female)"]
  FL_CAP = Capacitor Polarized [package=panasonic_e]
  PWR_CAP = Capacitor Polarized [package=panasonic_e]

nets:
  N1: FR_MOTOR.pin1, FR_DRIVER.OUT_2B
  N2: FR_MOTOR.pin2, FR_DRIVER.OUT_2A
  N3: FR_MOTOR.pin3, FR_DRIVER.OUT_1A
  N4: FR_MOTOR.pin4, FR_DRIVER.OUT_1B
  N5: BR_MOTOR.pin1, BR_DRIVER.OUT_2B
  N6: BR_MOTOR.pin2, BR_DRIVER.OUT_2A
  N7: BR_MOTOR.pin3, BR_DRIVER.OUT_1A
  N8: BR_MOTOR.pin4, BR_DRIVER.OUT_1B
  N9: FL_MOTOR.pin1, FL_DRIVER.OUT_2B
  N10: FL_MOTOR.pin2, FL_DRIVER.OUT_2A
  N11: FL_MOTOR.pin3, FL_DRIVER.OUT_1A
  N12: FL_MOTOR.pin4, FL_DRIVER.OUT_1B
  N13: BL_MOTOR.pin1, BL_DRIVER.OUT_2B
  N14: BL_MOTOR.pin2, BL_DRIVER.OUT_2A
  N15: BL_MOTOR.pin3, BL_DRIVER.OUT_1A
  N16: BL_MOTOR.pin4, BL_DRIVER.OUT_1B
  N17: FR_DRIVER.SLEEP, FR_DRIVER.VDD
  N18: FR_DRIVER.STEP, ARDUINO_MICRO2.D6
  N19: FR_DRIVER.DIR, ARDUINO_MICRO2.D5
  N20: FR_DRIVER.VMOT, FR_DRIVER.GROUND#141, BR_DRIVER.VMOT, FL_DRIVER.VMOT, FL_DRIVER.GROUND#141, BL_DRIVER.VMOT, BL_DRIVER.GROUND#141, MOTOR_PWR.pin1, MOTOR_PWR.pin2, BR_CAP.+, FR_CAP.+, FR_CAP.-, BL_CAP.+, BL_CAP.-, FL_CAP.+, FL_CAP.-
  N21: BR_DRIVER.SLEEP, BR_DRIVER.VDD
  N22: BR_DRIVER.STEP, ARDUINO_MICRO2.D8
  N23: BR_DRIVER.DIR, ARDUINO_MICRO2.D7
  N24: BR_DRIVER.GROUND#141, BR_CAP.-
  N25: FL_DRIVER.SLEEP, FL_DRIVER.VDD
  N26: FL_DRIVER.STEP, ARDUINO_MICRO2.D4
  N27: FL_DRIVER.DIR, ARDUINO_MICRO2.D3
  N28: BL_DRIVER.SLEEP, BL_DRIVER.VDD
  N29: BL_DRIVER.STEP, ARDUINO_MICRO2.D10
  N30: BL_DRIVER.DIR, ARDUINO_MICRO2.D9
  N31: +5V-2.pin1, +5V-1.pin1, +5V-3.pin1, +5V-4.pin1, +5V-5.pin1, ARDUINO_MICRO2.RST#5, AIN1.pin1, AIN2.pin1, AIN4.pin1, AIN5.pin1, AIN6.pin1, AIN3.pin1
  N32: +5V-2.pin2, +5V-1.pin2, +5V-3.pin2, +5V-4.pin2, +5V-5.pin2, ARDUINO_MICRO2.RST#30, AIN1.pin2, AIN2.pin2, AIN4.pin2, AIN5.pin2, AIN6.pin2, AIN3.pin2
  N33: ARDUINO_PWR.pin1, ARDUINO_MICRO2.GND#31, PWR_CAP.-
  N34: ARDUINO_PWR.pin2, ARDUINO_MICRO2.VIN, PWR_CAP.+
  N35: ARDUINO_MICRO2.GND#6, I2C_5V.pin1
  N36: ARDUINO_MICRO2.D2, I2C_5V.pin2
  N37: ARDUINO_MICRO2.A1, AIN1.pin3
  N38: ARDUINO_MICRO2.A2, AIN2.pin3
  N39: ARDUINO_MICRO2.A3, AIN3.pin3
  N40: ARDUINO_MICRO2.A4, AIN4.pin3
  N41: ARDUINO_MICRO2.A5, AIN5.pin3
  N42: ARDUINO_MICRO2.N/C#27, AIN6.pin3

custom parts:
  Arduino Micro: Arduino Micro Microcontroller
