# Fritzing sketch Compact redesign (saved by Fritzing 0.9.2b)
circuit board: 9cm x 5cm
breadboards: 1

parts:
  ARDUINO = mystery part, 34 pins [chip_label=12]
  7-10_VIN = male pin header, 2 pins [form="♂ (male)"]
  FL_MOTOR1 = male pin header, 4 pins [form="♂ (male)"]
  FL_DRIVER1 = mystery part, 16 pins [chip_label=?]
  FL_DRIVER2 = mystery part, 16 pins [chip_label=?]
  FL_DRIVER3 = mystery part, 16 pins [chip_label=?]
  FL_MOTOR2 = male pin header, 4 pins [form="♂ (male)"]
  FL_MOTOR3 = male pin header, 4 pins [form="♂ (male)"]
  C1 = Electrolytic Capacitor [capacitance=1µF package="100 mil [THT, electrolytic]"]
  C2 = Electrolytic Capacitor [capacitance=1µF package="100 mil [THT, electrolytic]"]
  C3 = Electrolytic Capacitor [capacitance=1µF package="100 mil [THT, electrolytic]"]

nets:
  N1: ARDUINO.pin33, FL_DRIVER1.pin16
  N2: ARDUINO.pin34, FL_DRIVER1.pin15
  N3: 7-10_VIN.pin1, FL_DRIVER1.pin8, FL_DRIVER2.pin8, FL_DRIVER3.pin8, C1.+, C2.+, C3.+
  N4: 7-10_VIN.pin2, FL_DRIVER1.pin7, FL_DRIVER2.pin7, FL_DRIVER3.pin7, C1.-, C2.-, C3.-
  N5: FL_MOTOR1.pin1, FL_DRIVER1.pin3
  N6: FL_MOTOR1.pin2, FL_DRIVER1.pin4
  N7: FL_MOTOR1.pin3, FL_DRIVER1.pin5
  N8: FL_MOTOR1.pin4, FL_DRIVER1.pin6
  N9: FL_DRIVER1.pin1, FL_DRIVER2.pin1, FL_DRIVER3.pin1
  N10: FL_DRIVER1.pin2, FL_DRIVER2.pin2, FL_DRIVER3.pin2
  N11: FL_DRIVER2.pin3, FL_MOTOR2.pin1
  N12: FL_DRIVER2.pin4, FL_MOTOR2.pin2
  N13: FL_DRIVER2.pin5, FL_MOTOR2.pin3
  N14: FL_DRIVER2.pin6, FL_MOTOR2.pin4
  N15: FL_DRIVER3.pin3, FL_MOTOR3.pin1
  N16: FL_DRIVER3.pin4, FL_MOTOR3.pin2
  N17: FL_DRIVER3.pin5, FL_MOTOR3.pin3
  N18: FL_DRIVER3.pin6, FL_MOTOR3.pin4

notes:
  -
  +
