# Fritzing sketch miniature redesign (saved by Fritzing 0.9.2b)
circuit board: 7.5cm x 5cm
breadboards: 1

parts:
  FL_DRIVER2 = mystery part, 16 pins [chip_label=?]
  FL_DRIVER3 = mystery part, 16 pins [chip_label=?]
  FL_MOTOR2 = male pin header, 4 pins [form="♂ (male)"]
  FL_MOTOR3 = male pin header, 4 pins [form="♂ (male)"]
  FL_MOTOR4 = male pin header, 4 pins [form="♂ (male)"]
  C2 = Electrolytic Capacitor [capacitance=1µF package="100 mil [THT, electrolytic]"]
  C3 = Electrolytic Capacitor [capacitance=1µF package="100 mil [THT, electrolytic]"]
  C1 = Electrolytic Capacitor [capacitance=1µF package="100 mil [THT, electrolytic]"]
  VIN = male pin header, 2 pins [form="♂ (male)"]
  Arduino_Micro = Arduino Micro (Rev3)
  SCL = male pin header, 2 pins [form="♂ (male)"]
  FL_DRIVER4 = mystery part, 16 pins [chip_label=?]
  E2 = male pin header, 2 pins [form="♂ (male)"]
  A1 = male pin header, 3 pins [form="♂ (male)"]
  A3 = male pin header, 3 pins [form="♂ (male)"]
  A5 = male pin header, 3 pins [form="♂ (male)"]
  E1 = male pin header, 2 pins [form="♂ (male)"]
  C3_2 = Electrolytic Capacitor [capacitance=1µF package="100 mil [THT, electrolytic]"]

nets:
  N1: FL_DRIVER2.pin1, FL_DRIVER2.pin7, FL_DRIVER3.pin1, FL_DRIVER3.pin7, C2.-, C3.-, C1.-, VIN.pin2, Arduino_Micro.GND, FL_DRIVER4.pin1, FL_DRIVER4.pin7, C3_2.-
  N2: FL_DRIVER2.pin2, FL_DRIVER3.pin2, Arduino_Micro.5V, FL_DRIVER4.pin2, A1.pin2, A3.pin2, A5.pin2
  N3: FL_DRIVER2.pin3, FL_MOTOR2.pin1
  N4: FL_DRIVER2.pin4, FL_MOTOR2.pin2
  N5: FL_DRIVER2.pin5, FL_MOTOR2.pin3
  N6: FL_DRIVER2.pin6, FL_MOTOR2.pin4
  N7: FL_DRIVER2.pin8, FL_DRIVER3.pin8, C2.+, C3.+, C1.+, FL_DRIVER4.pin8, E1.pin1
  N8: FL_DRIVER2.pin15, Arduino_Micro.D9_PWM/A9
  N9: FL_DRIVER2.pin16, Arduino_Micro.D8_PWM/A8
  N10: FL_DRIVER3.pin3, FL_MOTOR3.pin1
  N11: FL_DRIVER3.pin4, FL_MOTOR3.pin2
  N12: FL_DRIVER3.pin5, FL_MOTOR3.pin3
  N13: FL_DRIVER3.pin6, FL_MOTOR3.pin4
  N14: FL_DRIVER3.pin15, Arduino_Micro.D7
  N15: FL_DRIVER3.pin16, Arduino_Micro.D6_PWM/A7
  N16: FL_MOTOR4.pin1, FL_DRIVER4.pin3
  N17: FL_MOTOR4.pin2, FL_DRIVER4.pin4
  N18: FL_MOTOR4.pin3, FL_DRIVER4.pin5
  N19: FL_MOTOR4.pin4, FL_DRIVER4.pin6
  N20: VIN.pin1, E2.pin1, E1.pin2
  N21: Arduino_Micro.D2/SDA, SCL.pin2
  N22: Arduino_Micro.D3/SCL, SCL.pin1
  N23: Arduino_Micro.D4_PWM/A6, FL_DRIVER4.pin16
  N24: Arduino_Micro.D5_PWM, FL_DRIVER4.pin15
  N25: Arduino_Micro.VIN, E2.pin2, C3_2.+
  N26: Arduino_Micro.A5, A5.pin3
  N27: Arduino_Micro.A3, A3.pin3
  N28: Arduino_Micro.A1, A1.pin3
  N29: A1.pin1, A3.pin1, A5.pin1

notes:
  +
  SDA
