# Fritzing sketch power circuit (saved by Fritzing 0.9.2b)
circuit board: 5cm x 3cm
breadboards: 1

parts:
  WALL_POWER = female pin header, 2 pins [form="♀ (female)"]
  BATTERY = female pin header, 2 pins [form="♀ (female)"]
  S1 = SWITCH-DPDT [package=eg2211]
  D1 = Rectifier Diode [part_number=1N4001 package="300 mil [THT]"]
  D2 = Rectifier Diode [part_number=1N4001 package="300 mil [THT]"]
  VOUT-1 = female pin header, 2 pins [form="♀ (female)"]
  VOUT-2 = female pin header, 2 pins [form="♀ (female)"]
  VOUT-3 = female pin header, 2 pins [form="♀ (female)"]
  VOUT-4 = female pin header, 2 pins [form="♀ (female)"]
  VOUT-5 = female pin header, 2 pins [form="♀ (female)"]
  D3 = Rectifier Diode [part_number=1N4001 package="300 mil [THT]"]

nets:
  GND: WALL_POWER.pin1, BATTERY.pin1, D3.cathode
  N1: WALL_POWER.pin2, S1.5
  N2: BATTERY.pin2, S1.2
  N3: S1.1, D1.anode
  N4: S1.4, D2.anode
  N5: D1.cathode, D2.cathode, VOUT-1.pin2, VOUT-2.pin2, VOUT-3.pin2, VOUT-4.pin2, VOUT-5.pin2
  N6: VOUT-1.pin1, VOUT-2.pin1, VOUT-3.pin1, VOUT-4.pin1, VOUT-5.pin1, D3.anode
