# Fritzing sketch raspberry pi shield (saved by Fritzing 0.9.2b)
circuit board: 9.47897cm x 5.98263cm
breadboards: 1

parts:
  FL-C = Electrolytic Capacitor [capacitance=1µF package="100 mil [THT, electrolytic]"]
  C2 = Electrolytic Capacitor [capacitance=1µF package="100 mil [THT, electrolytic]"]
  C3 = Electrolytic Capacitor [capacitance=1µF package="100 mil [THT, electrolytic]"]
  BL_MOTOR = male pin header, 4 pins [form="♂ (male)"]
  FL_MOTOR = male pin header, 4 pins [form="♂ (male)"]
  FR_MOTOR = male pin header, 4 pins [form="♂ (male)"]
  FL_DRIVER = mystery part, 16 pins [chip_label=?]
  BL_DRIVER = mystery part, 16 pins [chip_label=?]
  FR_DRIVER = mystery part, 16 pins [chip_label=?]
  A0 = male pin header, 3 pins [form="♂ (male)"]
  ARDUINO = mystery part, 34 pins [chip_label=?]
  STEPPER_OPTIONS7 = male pin header, 4 pins [form="♂ (male)"]
  STEPPER_OPTIONS10 = male pin header, 4 pins [form="♂ (male)"]
  STEPPER_OPTIONS9 = male pin header, 4 pins [form="♂ (male)"]
  5V-I2C = male pin header, 2 pins [form="♂ (male)"]
  7-10V = male pin header, 2 pins [form="♂ (male)"]  # not connected

nets:
  N1: FL-C.-, FL_DRIVER.pin7
  N2: FL-C.+, FL_DRIVER.pin8
  N3: C2.-, BL_DRIVER.pin7
  N4: C2.+, BL_DRIVER.pin8
  N5: C3.-, FR_DRIVER.pin7
  N6: C3.+, FR_DRIVER.pin8
  N7: BL_MOTOR.pin1, BL_DRIVER.pin3
  N8: BL_MOTOR.pin2, BL_DRIVER.pin4
  N9: BL_MOTOR.pin3, BL_DRIVER.pin5
  N10: BL_MOTOR.pin4, BL_DRIVER.pin6
  N11: FL_MOTOR.pin1, FL_DRIVER.pin3
  N12: FL_MOTOR.pin2, FL_DRIVER.pin4
  N13: FL_MOTOR.pin3, FL_DRIVER.pin5
  N14: FL_MOTOR.pin4, FL_DRIVER.pin6
  N15: FR_MOTOR.pin1, FR_DRIVER.pin3
  N16: FR_MOTOR.pin2, FR_DRIVER.pin4
  N17: FR_MOTOR.pin3, FR_DRIVER.pin5
  N18: FR_MOTOR.pin4, FR_DRIVER.pin6
  N19: FL_DRIVER.pin1, BL_DRIVER.pin1, FR_DRIVER.pin1
  N20: FL_DRIVER.pin2, FL_DRIVER.pin14
  N21: FL_DRIVER.pin9, STEPPER_OPTIONS10.pin1
  N22: FL_DRIVER.pin10, STEPPER_OPTIONS10.pin2
  N23: FL_DRIVER.pin11, STEPPER_OPTIONS10.pin3
  N24: FL_DRIVER.pin12, STEPPER_OPTIONS10.pin4
  N25: BL_DRIVER.pin2, BL_DRIVER.pin14
  N26: BL_DRIVER.pin9, STEPPER_OPTIONS9.pin1
  N27: BL_DRIVER.pin10, STEPPER_OPTIONS9.pin2
  N28: BL_DRIVER.pin11, STEPPER_OPTIONS9.pin3
  N29: BL_DRIVER.pin12, STEPPER_OPTIONS9.pin4
  N30: FR_DRIVER.pin2, FR_DRIVER.pin14
  N31: FR_DRIVER.pin9, STEPPER_OPTIONS7.pin1
  N32: FR_DRIVER.pin10, STEPPER_OPTIONS7.pin2
  N33: FR_DRIVER.pin11, STEPPER_OPTIONS7.pin3
  N34: FR_DRIVER.pin12, STEPPER_OPTIONS7.pin4
  N35: A0.pin2, A0.pin3
  N36: ARDUINO.pin24, 5V-I2C.pin1
  N37: ARDUINO.pin25, 5V-I2C.pin2

notes:
  POWER SUPPLY CIRCUIT
  tim-doerzbacher.com
  SIG
  PWR
  GND
  SDA
  +
  -
