# Fritzing sketch power strip (saved by Fritzing 0.9.2b)
circuit board: 3.6cm x 2.5cm
breadboards: 1

parts:
  LOGIC5 = female pin header, 2 pins [form="♀ (female)"]
  LOGIC4 = female pin header, 4 pins [form="♀ (female)"]
  LOGIC6 = female pin header, 4 pins [form="♀ (female)"]
  LOGIC7 = female pin header, 2 pins [form="♀ (female)"]
  J14 = screw terminal, 2 pins
  J16 = screw terminal, 2 pins
  J15 = screw terminal, 2 pins
  J14_2 = screw terminal, 2 pins
  J13 = screw terminal, 2 pins

nets:
  N1: LOGIC5.pin1, LOGIC6.pin1, LOGIC6.pin2, LOGIC6.pin3, LOGIC6.pin4, J14.pin2, J15.pin2, J14_2.pin2, J13.pin2
  N2: LOGIC5.pin2, LOGIC7.pin2
  N3: LOGIC4.pin1, LOGIC4.pin2, LOGIC4.pin3, LOGIC4.pin4, J14.pin1, J16.pin1, J15.pin1, J14_2.pin1, J13.pin1
  N4: LOGIC7.pin1, J16.pin2

notes:
  +-
  - +
  + -
