# Fritzing sketch single stepper board (saved by Fritzing 0.9.2b)
circuit board: 3.5cm x 3.5cm
breadboards: 1

parts:
  C1 = Electrolytic Capacitor [capacitance=0.47mF voltage=35V package="100 mil [THT, electrolytic]"]
  C2 = Electrolytic Capacitor [capacitance=1µF package="100 mil [THT, electrolytic]"]
  M0 = female pin header, 3 pins [form="♀ (female)"]
  M1 = female pin header, 3 pins [form="♀ (female)"]
  J7 = Screw terminal - 2 pins [package=THT]
  U2 = mystery part, 16 pins [chip_label=STEPPER]
  LOGIC = female pin header, 4 pins [form="♀ (female)"]
  LOGIC1 = female pin header, 4 pins [form="♀ (female)"]

nets:
  N1: C1.-, J7.pin1, U2.pin7
  N2: C1.+, J7.pin2, U2.pin8
  N3: C2.-, M0.pin1, M1.pin1, U2.pin1, LOGIC.pin4
  N4: C2.+, M0.pin3, M1.pin3, U2.pin2, LOGIC.pin3
  N5: M0.pin2, U2.pin10
  N6: M1.pin2, U2.pin11
  N7: U2.pin3, LOGIC1.pin1
  N8: U2.pin4, LOGIC1.pin2
  N9: U2.pin5, LOGIC1.pin3
  N10: U2.pin6, LOGIC1.pin4
  N11: U2.pin15, LOGIC.pin2
  N12: U2.pin16, LOGIC.pin1

notes:
  GND
  5V
  STEP
  DIR
  7-10V
  MOTOR OUT
  DRV8834
