# Fritzing sketch trimotor holonomic mobo (saved by Fritzing 0.9.2b)
circuit board: 5.2cm x 4.5cm
breadboards: 1

parts:
  J8 = Screw terminal - 2 pins [package=THT]
  LOGIC1 = female pin header, 4 pins [form="♀ (female)"]
  LOGIC2 = female pin header, 4 pins [form="♀ (female)"]
  J9 = Screw terminal - 2 pins [package=THT]
  LOGIC3 = female pin header, 4 pins [form="♀ (female)"]
  J10 = Screw terminal - 2 pins [package=THT]
  LOGIC4 = female pin header, 2 pins [form="♀ (female)"]
  LOGIC5 = female pin header, 3 pins [form="♀ (female)"]
  J11 = Screw terminal - 2 pins [package=THT]
  C2 = Electrolytic Capacitor [capacitance=1µF package="100 mil [THT, electrolytic]"]
  Part1 = Arduino Micro (Rev3)
  LOGIC8 = female pin header, 3 pins [form="♀ (female)"]
  LOGIC9 = female pin header, 3 pins [form="♀ (female)"]
  LOGIC10 = female pin header, 3 pins [form="♀ (female)"]

nets:
  N1: J8.pin1, LOGIC1.pin4, LOGIC2.pin4, J9.pin1, LOGIC3.pin4, J10.pin1, LOGIC5.pin1, J11.pin1, C2.-, Part1.GND, LOGIC8.pin1, LOGIC9.pin1, LOGIC10.pin1
  N2: J8.pin2, J9.pin2, J10.pin2, J11.pin2, C2.+, Part1.VIN
  N3: LOGIC1.pin1, Part1.D9_PWM/A9
  N4: LOGIC1.pin2, Part1.D8_PWM/A8
  N5: LOGIC1.pin3, LOGIC2.pin3, LOGIC3.pin3, LOGIC5.pin2, Part1.5V, LOGIC8.pin2, LOGIC9.pin2, LOGIC10.pin2
  N6: LOGIC2.pin1, Part1.D7
  N7: LOGIC2.pin2, Part1.D6_PWM/A7
  N8: LOGIC3.pin1, Part1.D5_PWM
  N9: LOGIC3.pin2, Part1.D4_PWM/A6
  N10: LOGIC4.pin1, Part1.D2/SDA
  N11: LOGIC4.pin2, Part1.D3/SCL
  N12: LOGIC5.pin3, Part1.A1
  N13: Part1.A4, LOGIC10.pin3
  N14: Part1.A3, LOGIC9.pin3
  N15: Part1.A2, LOGIC8.pin3

notes:
  VIN
  SDA
  SCL
